# Fritzing sketch relay-driver (saved by Fritzing 0.9.4)
breadboards: 1

parts:
  Mod1 = Meadow F7 Micro
  Q1 = NPN-Transistor [package="TO92 [THT]"]
  U2 = RELAY [package=relay-g5q]
  R1 = Resistor [tolerance=±5% resistance=2.2k package=THT]
  D1 = Rectifier Diode [part_number=1N4001 package="300 mil [THT]"]
  VCC1 = Battery

nets:
  N1: Mod1.DO0, R1.Pin_1
  N2: Q1.E, VCC1.-
  N3: Q1.B, R1.Pin_0
  N4: Q1.C, U2.COIL1, D1.anode
  N5: U2.NC, D1.cathode, VCC1.+
