# Fritzing sketch temp-sensor (saved by Fritzing 0.9.4)
breadboards: 1

parts:
  Mod1 = Meadow F7 Micro
  R1 = Resistor [tolerance=±1% resistance=330 package=THT]
  R2 = Trimmer Potentiometer [maximum_resistance=10kΩ package=THT]

nets:
  N1: Mod1.3.3V, R1.Pin_1
  N2: Mod1.GND, R2.leg1
  N3: Mod1.A0, R1.Pin_0, R2.leg2
